# Fritzing sketch snakegame2 (saved by Fritzing 0.9.3b)
breadboards: 1

parts:
  Onderdeel1 = Arduino Leonardo (Rev3b)
  U1 = 74HC595 [package="DIP16 [THT]"]
  U2 = 74HC595 [package="DIP16 [THT]"]
  Disp1 = LBT2088AH [part_number=LBT2088AH]
  R1 = Resistor [tolerance=±5% resistance=220 package="0402 [SMD]"]
  R2 = Resistor [tolerance=±5% resistance=220 package="0402 [SMD]"]
  R3 = Resistor [tolerance=±5% resistance=220 package="0402 [SMD]"]
  R4 = Resistor [tolerance=±5% resistance=220 package="0402 [SMD]"]
  R5 = Resistor [tolerance=±5% resistance=220 package="0402 [SMD]"]
  R6 = Resistor [tolerance=±5% resistance=220 package="0402 [SMD]"]
  R7 = Resistor [tolerance=±5% resistance=220 package="0402 [SMD]"]
  R8 = Resistor [tolerance=±5% resistance=220 package="0402 [SMD]"]
  R9 = Resistor [tolerance=±5% resistance=10k package="0402 [SMD]"]
  R10 = Resistor [tolerance=±5% resistance=10k package="0402 [SMD]"]
  Onderdeel2 = Thumb Joystick

nets:
  N1: Onderdeel1.RESET, Onderdeel2.SEL
  VCC: Onderdeel1.5V, U1.MR, U1.VCC, U2.MR, U2.VCC, Onderdeel2.VCC
  GND: Onderdeel1.GND, R9.Pin_1, R10.Pin_1, Onderdeel2.GND
  N2: Onderdeel1.A4, Onderdeel2.VERT
  N3: Onderdeel1.A5, Onderdeel2.HORZ
  N4: Onderdeel1.D8/A8, U2.DS
  N5: Onderdeel1.D9_PWM/A9, U1.ST_CP, U2.ST_CP
  N6: Onderdeel1.D10_PWM/A10, U1.SH_CP, U2.SH_CP
  N7: U1.Q1, Disp1.pin_6
  N8: U1.Q2, Disp1.pin_5
  N9: U1.Q3, Disp1.pin_15
  N10: U1.Q4, Disp1.pin_3
  N11: U1.Q5, Disp1.pin_14
  N12: U1.Q6, Disp1.pin_10
  N13: U1.Q7, Disp1.pin_9
  N14: U1.GND, R9.Pin_0
  N15: U1.DS, U2.Q7'
  N16: U1.Q0, Disp1.pin_12
  N17: U2.Q1, R1.Pin_1
  N18: U2.Q2, R4.Pin_1
  N19: U2.Q3, R5.Pin_1
  N20: U2.Q4, R6.Pin_1
  N21: U2.Q5, R7.Pin_1
  N22: U2.Q6, R8.Pin_1
  N23: U2.Q7, R3.Pin_1
  N24: U2.GND, R10.Pin_0
  N25: U2.Q0, R2.Pin_1
  N26: Disp1.pin1, R4.Pin_0
  N27: Disp1.pin2, R7.Pin_0
  N28: Disp1.pin_4, R3.Pin_0
  N29: Disp1.pin_7, R8.Pin_0
  N30: Disp1.pin_8, R6.Pin_0
  N31: Disp1.pin_11, R1.Pin_0
  N32: Disp1.pin_13, R5.Pin_0
  N33: Disp1.pin_16, R2.Pin_0
